// Logisim project revisãoP1.circ as structural Verilog: 1 circuit, main circuit main
module main (
  input  in_1,
  input  in_2,
  input  A,
  input  B,
  input  Vai_um,
  input  in_6,
  input  in_7,
  input  in_8
);

  wire and_1_out, and_2_out, and_3_out, and_4_out, and_5_out, and_6_out, and_7_out, and_8_out, and_9_out,
       and_10_out, not_1_out, not_2_out, not_3_out, not_4_out, or_1_out, or_2_out, or_3_out, or_4_out,
       or_5_out, xor_1_out, xor_2_out;

  or or_1 (or_1_out, in_1, not_1_out);
  not not_1 (not_1_out, or_2_out);
  or or_2 (or_2_out, in_2, not_4_out);
  not not_2 (not_2_out, in_6);
  not not_3 (not_3_out, in_7);
  not not_4 (not_4_out, or_1_out);
  LED led_1 (.in(not_4_out));
  LED led_2 (.in(not_1_out));
  xor xor_1 (xor_1_out, A, B);
  not not_5 (not_3_out, in_8);
  and and_1 (and_1_out, xor_1_out, Vai_um);
  and and_2 (and_2_out, A, B);
  xor xor_2 (xor_2_out, xor_1_out, Vai_um);
  and and_3 (and_3_out, in_6, not_3_out, not_3_out);
  and and_4 (and_4_out, not_2_out, in_7, not_3_out);
  and and_5 (and_5_out, not_2_out, not_3_out, in_8);
  and and_6 (and_6_out, in_6, in_7, in_8);
  and and_7 (and_7_out, in_6, in_7, not_3_out);
  and and_8 (and_8_out, in_6, not_3_out, in_8);
  and and_9 (and_9_out, not_2_out, in_7, in_8);
  and and_10 (and_10_out, in_6, in_7, in_8);
  LED led_3 (.in(xor_2_out));
  LED led_4 (.in(or_3_out));
  or or_3 (or_3_out, and_1_out, and_2_out);
  or or_4 (or_4_out, and_3_out, and_4_out, and_5_out, and_6_out);
  or or_5 (or_5_out, and_7_out, and_8_out, and_9_out, and_10_out);
  LED led_5 (.in(or_4_out));
  LED led_6 (.in(or_5_out));
endmodule
